# Fritzing sketch viviware_Accelerometer (saved by Fritzing 0.9.3b)
breadboards: 1

parts:
  パーツ1 = Arduino Uno (Rev3)
  U3 = CMA3000-D01 [package=cma3000]

nets:
  N1: パーツ1.A0, U3.MOSI
  N2: パーツ1.A1, U3.CS
  N3: パーツ1.A2, U3.INT
  5V: パーツ1.5V, U3.VDD, U3.VSS
  N4: パーツ1.GND, U3.DVIO, U3.SCK

notes:
  KXR94-2050
