# Fritzing sketch viviware_button (saved by Fritzing 0.9.3b)
breadboards: 1

parts:
  パーツ1 = Arduino Uno (Rev3)
  S1 = Pushbutton [package="[THT]"]
  R2 = Resistor [tolerance=±5% resistance=10k package=THT]

nets:
  N1: パーツ1.GND, S1.Pin_1, S1.Pin_2
  N2: パーツ1.D2, S1.Pin_3, S1.Pin_4, R2.Pin_1
  N3: パーツ1.5V, R2.Pin_0

notes:
  （茶黒橙金）
