# Fritzing sketch viviware_led (saved by Fritzing 0.9.3b)
breadboards: 1

parts:
  パーツ1 = Arduino Uno (Rev3)
  LED1 = LED - 5mm [color="Red (633nm)" package="5 mm [THT]"]
  R1 = Resistor [tolerance=±5% resistance=330 package=THT]

nets:
  N1: パーツ1.D5_PWM, R1.Pin_1
  N2: パーツ1.GND, LED1.cathode
  N3: LED1.anode, R1.Pin_0

notes:
  （橙橙茶金）
