# Fritzing sketch viviware_pressure (saved by Fritzing 0.9.3b)
breadboards: 1

parts:
  パーツ1 = Arduino Uno (Rev3)
  R1 = Resistor [tolerance=±5% resistance=10k package=THT]
  J1 = Basic Force Sensing Resistor (FSR) [part_number=センサー package=THT]

nets:
  N1: パーツ1.A0, R1.Pin_0, J1.pin_1
  N2: パーツ1.GND, R1.Pin_1
  N3: パーツ1.5V, J1.pin_0

notes:
  （茶黒橙金）
